# Fritzing sketch layout (saved by Fritzing 0.9.3b)

parts:
  RFID-RC522 = RFID-RC522-v2
  LCD_16x2_i2C = LCD1602-I2C
  part = ESP32-38PinWide [part_number=ESP32-38PinWide]

nets:
  N1: RFID-RC522.SDA, part.GPIO5
  N2: RFID-RC522.SCK, part.GPIO18
  N3: RFID-RC522.MOSI, part.GPIO23
  N4: RFID-RC522.MISO, part.GPIO19
  GND: RFID-RC522.GND, part.GND
  N5: RFID-RC522.RST, part.GPIO2
  3.3V: RFID-RC522.3.3V, LCD_16x2_i2C.VCC, part.3.3
  N6: LCD_16x2_i2C.GND, part.GPIO11
  N7: LCD_16x2_i2C.SDA, part.GPIO21
  N8: LCD_16x2_i2C.SCL, part.GPIO22

custom parts:
  RFID-RC522-v2: A simple China made RFID-RC522 Reader; do check the pin labels, as this is a MFRC522 based clone.
  LCD1602-I2C: A standard character display, usually with 2x16 characters. Comes in many colors with LCM1602 IIC attached.
  ESP32-38PinWide: Generic 38-Pin ESP32 with wide format (only access to one side of pins on a breadboard) based on Stephen Lilley's HiLetgo ESP-WROOM-32 ESP32 ESP-32S Development Board.
